# Fritzing sketch ac (saved by Fritzing 0.9.5d)

parts:
  LED1 = LEDs [package=led10mm]
  Q1 = NPN-Transistor [package="TO92 [THT]"]
  R1 = Resistor [tolerance=±5% resistance=470 package="0603 [SMD]"]
  M1 = Arduino NANO RP2040 CONNECT with headers
  AM1 = AM2320 Humidity and Temperature Sensor [part_number="Adafruit #3721"]

nets:
  N1: LED1.C, Q1.C, M1.GND-4, M1.GND-29
  N2: LED1.A, Q1.E, M1.+5V
  N3: Q1.B, R1.Pin_1
  N4: R1.Pin_0, M1.D10
  N5: M1.D15, AM1.SDA

notes:
  ac control
  transistor
  5v - colector
  data - base
  gnd - emitter

custom parts:
  Arduino NANO RP2040 CONNECT with headers: Meet the only connected RP2040 board. It fits the Arduino Nano form factor, making it a small board with BIG features. The brain of the board is the Raspberry Pi RP2040 silicon; a dual-core Arm Cortex M0+ running at 133MHz. It has 264KB of SRAM, and the 16MB of flash memory is off-chip to give you extra storage. But what’s really exciting is the on-board connectivity options. The hugely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
  AM2320 Humidity and Temperature Sensor: AM2320 I2C Humidity and Temperature Sensor
